# Fritzing sketch MemoryGame (saved by Fritzing 1.0.7)
breadboards: 1

parts:
  Part1 = Arduino Nano (Rev3.0)
  SW1 = Tactile Switch 2-pin [package=THT]
  SW2 = Tactile Switch 2-pin [package=THT]
  SW3 = Tactile Switch 2-pin [package=THT]
  SW4 = Tactile Switch 2-pin [package=THT]
  SW5 = Tactile Switch 2-pin [package=THT]
  SW6 = Tactile Switch 2-pin [package=THT]
  OLED1 = 0.96in SSD1306 I2C OLED 128x64
  LED_MATRIX1 = WS2812B 4x4 RGB Matrix — Flying Leads
  Mod1 = Passive Buzzer

nets:
  N1: Part1.GND, SW4.1, Mod1.-
  N2: Part1.D2, SW5.2
  GND: Part1.D3, SW2.1, SW3.1, SW5.1, SW6.1, OLED1.GND, LED_MATRIX1.GND
  N3: Part1.D4, SW1.1
  N4: Part1.D5, SW2.2
  N5: Part1.D6, SW6.2
  N6: Part1.D7, LED_MATRIX1.DIN
  5V: Part1.5V, OLED1.VCC, LED_MATRIX1.V+
  N7: Part1.A5, OLED1.SCL
  N8: Part1.A4, OLED1.SDA
  N9: Part1.A2, Mod1.S

custom parts:
  Tactile Switch 2-pin: Generic 2-pin breadboard tactile switch, 5.08mm lead pitch, momentary normally-open.
  0.96in SSD1306 I2C OLED 128x64: 0.96 inch 128x64 SSD1306 I2C OLED module on the common blue 27.3 x 27.8 mm PCB. Four-pin 2.54 mm header: GND, VCC, SCL, SDA. Typical I2C address 0x3C.
  WS2812B 4x4 RGB Matrix — Flying Leads: 4x4 matrix of 16 WS2812B addressable RGB LEDs on a nominal 30 mm square HW-2812B-16-style board. Breadboard view uses four bendable flying leads. DIN and V+ are on the input side; DOUT and GND are on the opposite side for easy cascading.
