# Fritzing sketch MemoryGamePCB (saved by Fritzing 1.0.7)
circuit board: 6.54604cm x 7.3623cm
breadboards: 1

parts:
  Nano = Arduino Nano (Rev3.0)
  Up = Tactile Switch 2-pin [package=THT]
  Left = Tactile Switch 2-pin [package=THT]
  Right = Tactile Switch 2-pin [package=THT]
  Down = Tactile Switch 2-pin [package=THT]
  Start = Tactile Switch 2-pin [package=THT]
  Select = Tactile Switch 2-pin [package=THT]
  Buzzer = Passive Buzzer
  Matrix = Header 3 [package=molex-1x3_lock]
  Oled = polarizedheader 4pin 0.156in [package=THT]

nets:
  N1: Nano.GND, Up.2, Left.1, Right.1, Down.1, Start.1, Select.1, Buzzer.-, Matrix.1, Oled.pin1
  N2: Nano.D2, Start.2
  N3: Nano.D3, Right.2
  N4: Nano.D4, Up.1
  N5: Nano.D5, Left.2
  N6: Nano.D6, Select.2
  N7: Nano.D7, Matrix.3
  N8: Nano.D8, Down.2
  N9: Nano.5V, Matrix.2, Oled.pin2
  N10: Nano.A5, Oled.pin4
  N11: Nano.A4, Oled.pin3
  N12: Nano.A2, Buzzer.S

notes:
  Buzzer

custom parts:
  Tactile Switch 2-pin: Generic 2-pin breadboard tactile switch, 5.08mm lead pitch, momentary normally-open.
